# Fritzing sketch Assignment2_sketch (saved by Fritzing 0.9.3b)
breadboards: 1

parts:
  LED16 = smd LED [color="Yellow (574nm)" package="1206 [SMD]"]
  R1 = Resistor [tolerance=±5% resistance=220 package=THT]
  R2 = Resistor [tolerance=±5% resistance=220 package=THT]
  R3 = Resistor [tolerance=±5% resistance=220 package=THT]
  R4 = Resistor [tolerance=±5% resistance=220 package=THT]
  R5 = Resistor [tolerance=±5% resistance=220 package=THT]
  R6 = Resistor [tolerance=±5% resistance=220 package=THT]
  R7 = Resistor [tolerance=±5% resistance=220 package=THT]
  R8 = Resistor [tolerance=±5% resistance=220 package=THT]
  R9 = Resistor [tolerance=±5% resistance=220 package=THT]
  R10 = Resistor [tolerance=±5% resistance=220 package=THT]
  R11 = Resistor [tolerance=±5% resistance=220 package=THT]
  R12 = Resistor [tolerance=±5% resistance=220 package=THT]
  R13 = Resistor [tolerance=±5% resistance=220 package=THT]
  R14 = Resistor [tolerance=±5% resistance=220 package=THT]
  R15 = Resistor [tolerance=±5% resistance=220 package=THT]
  R16 = Resistor [tolerance=±5% resistance=220 package=THT]
  R17 = Resistor [tolerance=±5% resistance=220 package=THT]
  R18 = Resistor [tolerance=±5% resistance=220 package=THT]
  LED17 = smd LED [color="Green (570nm)" package="1206 [SMD]"]
  LED18 = smd LED [color="Green (570nm)" package="1206 [SMD]"]
  LED19 = smd LED [color="Yellow (574nm)" package="1206 [SMD]"]
  LED20 = smd LED [color="Green (570nm)" package="1206 [SMD]"]
  LED21 = smd LED [color="Yellow (574nm)" package="1206 [SMD]"]
  LED22 = smd LED [color="Green (570nm)" package="1206 [SMD]"]
  LED23 = smd LED [color="Yellow (574nm)" package="1206 [SMD]"]
  LED26 = smd LED [color="Green (570nm)" package="1206 [SMD]"]
  LED27 = smd LED [color="Yellow (574nm)" package="1206 [SMD]"]
  LED34 = smd LED [color="Green (570nm)" package="1206 [SMD]"]
  LED35 = smd LED [color="Green (570nm)" package="1206 [SMD]"]
  LED36 = smd LED [color="Green (570nm)" package="1206 [SMD]"]
  LED37 = smd LED [color="Yellow (574nm)" package="1206 [SMD]"]
  LED38 = smd LED [color="Yellow (574nm)" package="1206 [SMD]"]
  LED39 = smd LED [color="Yellow (574nm)" package="1206 [SMD]"]
  Part1 = Arduino BT
  LED40 = smd LED [color="Green (570nm)" package="1206 [SMD]"]
  LED41 = smd LED [color="Yellow (574nm)" package="1206 [SMD]"]

nets:
  N1: LED16.cathode, LED17.cathode, LED18.cathode, LED19.cathode, LED20.cathode, LED21.cathode
  N2: LED16.anode, R14.Pin_0
  N3: R1.Pin_0, Part1.D2
  N4: R1.Pin_1, LED22.anode
  N5: R2.Pin_0, Part1.D4
  N6: R2.Pin_1, LED40.anode
  N7: R3.Pin_1, LED26.anode
  N8: R4.Pin_0, LED27.anode
  N9: R5.Pin_0, LED41.anode
  N10: R6.Pin_0, LED23.anode
  N11: R6.Pin_1, Part1.PWM_D3
  N12: R7.Pin_0, LED39.anode
  N13: R8.Pin_0, LED38.anode
  N14: R9.Pin_0, LED37.anode
  N15: R10.Pin_1, LED36.anode
  N16: R11.Pin_1, LED35.anode
  N17: R12.Pin_1, LED34.anode
  N18: R13.Pin_1, LED17.anode
  N19: R15.Pin_1, LED18.anode
  N20: R16.Pin_0, LED19.anode
  N21: R17.Pin_1, LED20.anode
  N22: R18.Pin_0, LED21.anode, LED22.cathode, LED23.cathode, LED26.cathode, LED27.cathode, LED34.cathode, LED35.cathode, LED36.cathode, LED37.cathode, LED38.cathode, LED39.cathode, Part1.GND, LED40.cathode, LED41.cathode
